# Fritzing sketch schematic (saved by Fritzing 0.9.3b)
circuit board: 8.46667cm x 5.64444cm
breadboards: 1

parts:
  R1 = Resistor [tolerance=±5% resistance=1k package=THT]
  U1 = FS1000A - 433Mhz RF Transmitter [package=THT]
  LED1 = smd LED [color="Green (570nm)" part_number=RX package="0603 [SMD]"]
  LED2 = smd LED [color="Red (635nm)" part_number=TX package="0603 [SMD]"]
  R2 = Resistor [tolerance=±5% resistance=1k package=THT]
  U2 = RF-LINK_RX [package=rf-link_rx]
  Arduino = Arduino Nano (Rev3.0)
  S2 = Pushbutton [package="[THT]"]
  ANT1 = Antenna
  ANT2 = Antenna

nets:
  N1: R1.Pin_0, LED1.anode
  N2: R1.Pin_1, Arduino.D3
  N3: U1.DATA, Arduino.D10
  5V: U1.VCC, U2.+5V, Arduino.5V
  GND: U1.GND, LED1.cathode, LED2.cathode, U2.GND, Arduino.GND, S2.Pin_1, S2.Pin_2
  N4: U1.Antenna, ANT2.antenna_lead
  N5: LED2.anode, R2.Pin_0
  N6: R2.Pin_1, Arduino.D4
  N7: U2.DATA, Arduino.D2
  N8: U2.ANT, ANT1.antenna_lead
  N9: Arduino.D6, S2.Pin_3, S2.Pin_4

custom parts:
  FS1000A - 433Mhz RF Transmitter: This is 433Mhz RF transmitter with receiver kit for Arduino ARM MCU wireless Application environment: Remote control switch, receiver module, motorcycles, automobile anti-theft products, home security products, electric doors, shutter doors, windows, remote control socket, remote control LED, remote audio remote control electric doors, garage door remote control, remote control retractable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
